# Fritzing sketch Herz (saved by Fritzing 0.9.10b)

parts:
  Bauteil1 = Adafruit ESP32 Feather V2
  U1 = LIPO-1000mAh [package=lipo-1000]
  S3 = SWITCH_SPDT [package=kps-1290]
  Bauteil2 = NeoPixel Jewel [part_number=2226]
  MOTOR1 = Vibration Motor
  Q1 = TRANSISTOR_NPN [package=to-92-ammo]
  R1 = Resistor [tolerance=±5% resistance=220 package="0402 [SMD]"]

nets:
  GND: Bauteil1.GND, U1.-, Bauteil2.GND
  N1: Bauteil1.VBAT, S3.P, Bauteil2.VDD
  N2: Bauteil1.IO15_A8, R1.Pin_0
  N3: Bauteil1.IO14_A6, Bauteil2.IN
  N4: U1.+, S3.O
  N5: MOTOR1.NEG, Q1.E
  N6: Q1.B, R1.Pin_1

custom parts:
  NeoPixel Jewel: We fit seven of our tiny 5050 (5mm x 5mm) smart RGB LEDs onto a beautiful, round PCB with mounting holes and a chainable design to create what we think is our most elegant (and evening-wear appropriate) NeoPixel board yet. Use only one microcontroller pin to control as many as you can chain together! Each LED is addressable as the driver chip is inside the LED. Each one has ~18mA constant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
  Vibration Motor: An eccentric vibration motor!
